# Fritzing sketch Arduino-Example-Wiring (saved by Fritzing 0.9.3b)

parts:
  Bauteil1 = Analog Digital MUX Breakout
  Bauteil2 = Arduino Uno (Rev3)
  Bauteil3 = Arduino Can-Bus Shield
  T2 = LM35 Temperature Sensor [package="TO92 [THT]"]
  WeMos_D1_Mini_Relay_Shield_V1 = WeMos D1 Mini Relay Shield V2
  Bauteil4 = Bluetooth HC-05 Macho
  T3 = LM35 Temperature Sensor [package="TO92 [THT]"]
  Hall_effect_sensor = mystery part, 3 pins [chip_label=Hall]
  R1 = Resistor [tolerance=±5% resistance=10k package=THT]
  R2 = Resistor [tolerance=±5% resistance=22k package=THT]

nets:
  N1: Bauteil1.S0, Bauteil2.D4
  N2: Bauteil1.S1, Bauteil2.D5_PWM
  N3: Bauteil1.S2, Bauteil2.D6_PWM
  N4: Bauteil1.S3, Bauteil2.D7
  N5: Bauteil1.SIG, Bauteil2.A0
  N6: Bauteil2.A1, T2.Vout
  N7: Bauteil2.A2, T3.Vout
  N8: Bauteil2.A3, Hall_effect_sensor.pin2
  N9: Bauteil2.D8, Bauteil4.TXD
  N10: Bauteil2.D9_PWM, R1.Pin_0
  N11: Bauteil2.D10_PWM/SS, Bauteil3.CAN_CS
  N12: Bauteil2.D11_PWM/MOSI, Bauteil3.MOSI
  N13: Bauteil2.D12/MISO, Bauteil3.MISO
  N14: Bauteil2.D13/SCK, Bauteil3.SCK
  N15: Bauteil2.D2, Bauteil3.CAN_INT
  N16: Bauteil2.D3_PWM, WeMos_D1_Mini_Relay_Shield_V1.D1
  N17: Bauteil2.GND, R2.Pin_1
  N18: Bauteil4.RXD, R1.Pin_1, R2.Pin_0

notes:
  →3MW (ECU_OK)
  ←Cell voltage probes
  ←Pack temperature (front)
  →CAN-Bus
  Bluetooth
  ←Pack temperature (rear)
  (i.e. voltage dividers)
  ←Pack current
