# Fritzing sketch Arduino-Example-Yazaki-Relays (saved by Fritzing 0.9.3b)

parts:
  Bauteil1 = Analog Digital MUX Breakout
  Bauteil2 = Arduino Uno (Rev3)
  Bauteil3 = Arduino Can-Bus Shield
  T2 = LM35 Temperature Sensor [package="TO92 [THT]"]
  WeMos_D1_Mini_Relay_Shield_V1 = WeMos D1 Mini Relay Shield V2
  Bauteil4 = Bluetooth HC-05 Macho
  T3 = LM35 Temperature Sensor [package="TO92 [THT]"]
  Hall_effect_sensor = mystery part, 3 pins [chip_label=Hall]
  Power_Regulator_5V = Breadboard Power Supply Board SMD
  Yazaki_12_pin = Camdenboss CTB0158-12 [part_number=CTB0158-12 package=THT]
  D1 = Rectifier Diode [part_number=1N4001 package="Melf DO-213 AB [SMD]"]
  R1 = Resistor [tolerance=±5% resistance=470 package="0603 [SMD]"]
  K2_Charge_Relay_450V_40A = CAR RELAY [package=THT]
  K1_Sevcon_Logic_Supply_450V_10A = CAR RELAY [package=THT]
  K3_Main_Relay_450V_150A = CAR RELAY [package=THT]
  U1 = Mystery Part - 3 pins [chip_label=? package=THT]  # not connected
  U2 = LIPO-1000mAh [package=lipo-1000]
  Yazaki_12_pin1 = Camdenboss CTB0158-2 [part_number=CTB0158-2 package=THT]
  F1_(5A) = FUSE [package=fuse_5mm]
  F3_(500A) = FUSE [package=fuse_5mm]
  F2_(50A) = FUSE [package=fuse_5mm]

nets:
  VCC: Bauteil1.VCC, Bauteil1.EN, Bauteil2.5V, Bauteil3.VCC
  N1: Bauteil1.S0, Bauteil2.D4
  N2: Bauteil1.S1, Bauteil2.D5_PWM
  N3: Bauteil1.S2, Bauteil2.D6_PWM
  N4: Bauteil1.S3, Bauteil2.D7
  N5: Bauteil1.SIG, Bauteil2.A0
  N6: Bauteil2.A1, T2.Vout
  N7: Bauteil2.A2, T3.Vout
  N8: Bauteil2.A3, Hall_effect_sensor.pin2
  N9: Bauteil2.D8, Bauteil4.TXD
  N10: Bauteil2.D9_PWM, Bauteil4.RXD
  N11: Bauteil2.D10_PWM/SS, Bauteil3.CAN_CS
  N12: Bauteil2.D11_PWM/MOSI, Bauteil3.MOSI
  N13: Bauteil2.D12/MISO, Bauteil3.MISO
  N14: Bauteil2.D13/SCK, Bauteil3.SCK
  N15: Bauteil2.D2, Bauteil3.CAN_INT
  N16: Bauteil2.D3_PWM, WeMos_D1_Mini_Relay_Shield_V1.D1
  3V3: Bauteil2.3V3, Bauteil4.VCC
  GND: Bauteil2.GND, Bauteil3.GND
  N17: Bauteil3.CANH, Yazaki_12_pin.terminal_9
  N18: Bauteil3.CANL, Yazaki_12_pin.terminal_8
  N19: WeMos_D1_Mini_Relay_Shield_V1.COM, R1.Pin_1
  N20: WeMos_D1_Mini_Relay_Shield_V1.NO, Yazaki_12_pin.terminal_7
  GND_2: Bauteil4.GND, Power_Regulator_5V.GND, Yazaki_12_pin.terminal_12
  N21: Power_Regulator_5V.VIN, Yazaki_12_pin.terminal_2, R1.Pin_0
  N22: Yazaki_12_pin.terminal_1, D1.anode, K3_Main_Relay_450V_150A.85
  N23: Yazaki_12_pin.terminal_3, D1.cathode, K3_Main_Relay_450V_150A.86
  N24: Yazaki_12_pin.terminal_4, K1_Sevcon_Logic_Supply_450V_10A.86
  N25: Yazaki_12_pin.terminal_5, K2_Charge_Relay_450V_40A.85
  N26: Yazaki_12_pin.terminal_6, K2_Charge_Relay_450V_40A.86, K1_Sevcon_Logic_Supply_450V_10A.85
  N27: Yazaki_12_pin.terminal_10, K1_Sevcon_Logic_Supply_450V_10A.87
  N28: K2_Charge_Relay_450V_40A.30, F2_(50A).1
  N29: K1_Sevcon_Logic_Supply_450V_10A.30, F1_(5A).1
  N30: K3_Main_Relay_450V_150A.30, F3_(500A).2
  N31: U2.+, Yazaki_12_pin1.pin1
  N32: U2.-, Yazaki_12_pin1.pin2
  N33: Yazaki_12_pin1.terminal_1, F1_(5A).2, F3_(500A).1, F2_(50A).2

notes:
  3MW Relais
  ←Cell voltage probes
  ←Pack temperature (front)
  Bluetooth
  ←Pack temperature (rear)
  (i.e. voltage dividers)
  ←Pack current
  →PIN 3 Sevcon Logic Supply 48V
  →PIN 4 CAN-High
  →PIN 5 CAN-Low
  →PIN 6 ECU OK (3MW)
  →PIN 7 Relay Common
  →PIN 8 Relay Charger 40A
  →PIN 9 Relay Sevcon Supply 10A
  →PIN 10 12V Auxil-Perm
  →PIN 11 12V BMS
  →PIN 12 Main Relay
  →PIN 1 GND
  12V→5V
  MAIN
  BATTERY
  48V
  SEVCON 48V←
  CHARGER 48V→
  GND

custom parts:
  Mystery Part - 3 pins: A dummy, proxy, ersatz, stand-in part for whatever you want. With 3 pins on a 100 mil inline pin header footprint.
